# Fritzing sketch examplecircuit (saved by Fritzing 0.8.7b)

parts:
  BAT2 = Battery Holders [package=battery-aa]
  part = LED - 5mm [color="Red (633nm)" package="5 mm [THT]"]

nets:
  N1: BAT2.-, part.anode
  N2: BAT2.+, part.cathode
