# Fritzing sketch ledcircuitwithbutton (saved by Fritzing 0.8.7b)
breadboards: 1

parts:
  LED1 = LED - 5mm [color="White (4500K)" package="5 mm [THT]"]
  R1 = Resistor [tolerance=±5% resistance=330 package=THT]
  VCC1 = Battery
  S1 = Pushbutton [package="[THT]"]

nets:
  N1: LED1.cathode, S1.Pin_1, S1.Pin_2
  N2: R1.Pin_0, S1.Pin_3, S1.Pin_4
  N3: R1.Pin_1, VCC1.-
