# Fritzing sketch parallelleds (saved by Fritzing 0.8.7b)
breadboards: 1

parts:
  LED1 = LED - 5mm [color="White (4500K)" package="5 mm [THT]"]
  R1 = Resistor [tolerance=±5% resistance=330 package=THT]
  VCC1 = Battery
  LED2 = LED - 5mm [color="White (4500K)" package="5 mm [THT]"]

nets:
  N1: LED1.cathode, R1.Pin_0, LED2.cathode
  N2: LED1.anode, VCC1.+, LED2.anode
  N3: R1.Pin_1, VCC1.-
