# Fritzing sketch servos (saved by Fritzing 0.8.7b)
breadboards: 1

parts:
  VCC1 = 4 x AAA Battery Mount
  J1 = Basic Servo
  Part4 = Arduino Nano (Rev3.0)
  J2 = Basic Servo

nets:
  GND: VCC1.-, J1.gnd, Part4.GND, J2.gnd
  VCC: VCC1.+, J1.vcc, J2.vcc
  N1: J1.pulse, Part4.D9
  N2: Part4.D10, J2.pulse
