# Fritzing sketch ultrasonic (saved by Fritzing 0.8.7b)
breadboards: 1

parts:
  Part2 = SRF05 Ultrasonic Rangefinder
  Part3 = Arduino Nano (Rev3.0)

nets:
  VCC: Part2.VCC, Part3.5V
  N1: Part2.Trig, Part2.Echo, Part3.D7
  GND: Part2.GND, Part3.GND
